# Fritzing sketch Board (saved by Fritzing 0.9.2b)
breadboards: 3

parts:
  Part1 = Arduino Due (Rev2b)
  Q1 = PNP-Transistor [package="TO92 [THT]"]
  Q2 = PNP-Transistor [package="TO92 [THT]"]
  VCC1 = Battery
  7_Segment3 = 7 Segment Display
  7_Segment4 = 7 Segment Display
  R1 = Resistor [tolerance=±5% resistance=100 package=THT]
  R2 = Resistor [tolerance=±5% resistance=100 package=THT]
  Q3 = PNP-Transistor [package="TO92 [THT]"]
  Q4 = PNP-Transistor [package="TO92 [THT]"]
  Q5 = PNP-Transistor [package="TO92 [THT]"]
  Q6 = PNP-Transistor [package="TO92 [THT]"]
  Q7 = PNP-Transistor [package="TO92 [THT]"]
  R3 = Resistor [tolerance=±5% resistance=100 package=THT]
  R4 = Resistor [tolerance=±5% resistance=100 package=THT]
  R5 = Resistor [tolerance=±5% resistance=100 package=THT]
  R6 = Resistor [tolerance=±5% resistance=100 package=THT]
  R7 = Resistor [tolerance=±5% resistance=100 package=THT]
  R8 = Resistor [tolerance=±5% resistance=120 package=THT]
  R9 = Resistor [tolerance=±5% resistance=120 package=THT]
  R10 = Resistor [tolerance=±5% resistance=120 package=THT]
  R11 = Resistor [tolerance=±5% resistance=120 package=THT]
  R12 = Resistor [tolerance=±5% resistance=120 package=THT]
  R13 = Resistor [tolerance=±5% resistance=120 package=THT]
  R14 = Resistor [tolerance=±5% resistance=120 package=THT]
  Q8 = PNP-Transistor [package="TO92 [THT]"]
  Q9 = PNP-Transistor [package="TO92 [THT]"]
  Q10 = PNP-Transistor [package="TO92 [THT]"]
  Q11 = PNP-Transistor [package="TO92 [THT]"]
  Q12 = PNP-Transistor [package="TO92 [THT]"]
  Q13 = PNP-Transistor [package="TO92 [THT]"]
  Q14 = PNP-Transistor [package="TO92 [THT]"]
  Q15 = PNP-Transistor [package="TO92 [THT]"]
  Q16 = PNP-Transistor [package="TO92 [THT]"]
  Q17 = PNP-Transistor [package="TO92 [THT]"]
  Q18 = PNP-Transistor [package="TO92 [THT]"]
  Q19 = PNP-Transistor [package="TO92 [THT]"]
  Q20 = PNP-Transistor [package="TO92 [THT]"]
  Q21 = PNP-Transistor [package="TO92 [THT]"]
  Q22 = PNP-Transistor [package="TO92 [THT]"]
  R15 = Resistor [tolerance=±5% resistance=120 package=THT]
  R16 = Resistor [tolerance=±5% resistance=120 package=THT]
  R17 = Resistor [tolerance=±5% resistance=120 package=THT]
  R18 = Resistor [tolerance=±5% resistance=120 package=THT]
  R19 = Resistor [tolerance=±5% resistance=120 package=THT]
  R20 = Resistor [tolerance=±5% resistance=120 package=THT]
  R21 = Resistor [tolerance=±5% resistance=120 package=THT]
  R22 = Resistor [tolerance=±5% resistance=120 package=THT]
  R23 = Resistor [tolerance=±5% resistance=120 package=THT]
  R24 = Resistor [tolerance=±5% resistance=120 package=THT]
  R25 = Resistor [tolerance=±5% resistance=120 package=THT]
  R26 = Resistor [tolerance=±5% resistance=120 package=THT]
  R27 = Resistor [tolerance=±5% resistance=120 package=THT]
  R28 = Resistor [tolerance=±5% resistance=120 package=THT]
  R29 = Resistor [tolerance=±5% resistance=120 package=THT]
  R30 = Resistor [tolerance=±5% resistance=100 package=THT]
  R31 = Resistor [tolerance=±5% resistance=100 package=THT]
  R32 = Resistor [tolerance=±5% resistance=100 package=THT]
  R33 = Resistor [tolerance=±5% resistance=100 package=THT]
  R34 = Resistor [tolerance=±5% resistance=100 package=THT]
  R35 = Resistor [tolerance=±5% resistance=100 package=THT]
  R36 = Resistor [tolerance=±5% resistance=100 package=THT]
  R37 = Resistor [tolerance=±5% resistance=100 package=THT]
  R38 = Resistor [tolerance=±5% resistance=100 package=THT]
  R39 = Resistor [tolerance=±5% resistance=100 package=THT]
  R40 = Resistor [tolerance=±5% resistance=100 package=THT]
  R41 = Resistor [tolerance=±5% resistance=100 package=THT]
  R42 = Resistor [tolerance=±5% resistance=100 package=THT]
  R43 = Resistor [tolerance=±5% resistance=100 package=THT]
  R44 = Resistor [tolerance=±5% resistance=100 package=THT]
  S1 = Pushbutton [package="[THT]"]
  R45 = Resistor [tolerance=±5% resistance=10k package=THT]
  J1 = male pin header, 7 pins [form="♂ (male)"]
  R49 = Resistor [tolerance=±5% resistance=10k package=THT]
  R50 = Resistor [tolerance=±5% resistance=10k package=THT]
  R51 = Resistor [tolerance=±5% resistance=10k package=THT]
  R52 = Resistor [tolerance=±5% resistance=10k package=THT]
  7_Segment1 = 7 Segment Display  # not connected
  J2 = male pin header, 2 pins [form="♂ (male)"]
  J3 = male pin header, 8 pins [form="♂ (male)"]
  J4 = male pin header, 8 pins [form="♂ (male)"]  # not connected
  J5 = male pin header, 8 pins [form="♂ (male)"]  # not connected

nets:
  N1: Part1.D18/TX1, R23.Pin_1
  N2: Part1.D19/RX1, R24.Pin_1
  N3: Part1.D21/SCL3, R25.Pin_1
  N4: Part1.VIN, VCC1.+, J2.pin2
  N5: Part1.D2_PWM, R8.Pin_1
  N6: Part1.D3_PWM, R9.Pin_1
  N7: Part1.D5_PWM, R11.Pin_1
  N8: Part1.D6_PWM, R10.Pin_1
  N9: Part1.D7_PWM, R12.Pin_1
  N10: Part1.5V, R17.Pin_1, S1.Pin_1, S1.Pin_2, J1.pin2
  N11: Part1.D22, R26.Pin_1
  N12: Part1.D24, R27.Pin_1
  N13: Part1.D26, R28.Pin_1
  N14: Part1.D28, R29.Pin_1
  N15: Part1.D32, R15.Pin_1
  N16: Part1.D34, R16.Pin_1
  N17: Part1.D38, R18.Pin_1
  N18: Part1.D40, R19.Pin_1
  N19: Part1.D42, R20.Pin_1
  N20: Part1.D44, R21.Pin_1
  N21: Part1.D46, R22.Pin_1
  N22: Part1.D47, J1.pin6, R49.Pin_0
  N23: Part1.D48, R13.Pin_1
  N24: Part1.D49, J1.pin5, R52.Pin_0
  N25: Part1.D50, R14.Pin_1
  N26: Part1.D51, J1.pin4, R51.Pin_0
  N27: Part1.D52, S1.Pin_4, R45.Pin_0
  N28: Part1.D53, J1.pin3, R50.Pin_0
  N29: Part1.GND, VCC1.-, 7_Segment3.common_anode, 7_Segment4.common_anode, R45.Pin_1, J1.pin1, R49.Pin_1, R50.Pin_1, R51.Pin_1, R52.Pin_1, J2.pin1
  N30: Q1.B, R8.Pin_0
  N31: Q1.C, R1.Pin_0
  N32: Q2.B, R9.Pin_0
  N33: Q2.C, R2.Pin_0
  N34: 7_Segment3.Segment_F, R43.Pin_1
  N35: 7_Segment3.Segment_E, R42.Pin_1
  N36: 7_Segment3.Segment_D, R41.Pin_1
  N37: 7_Segment3.Segment_DP, R40.Pin_1
  N38: 7_Segment3.Segment_B, R39.Pin_1
  N39: 7_Segment3.Segment_A, R38.Pin_1
  N40: 7_Segment4.Segment_G, R37.Pin_1
  N41: 7_Segment4.Segment_F, R36.Pin_1
  N42: 7_Segment4.Segment_E, R35.Pin_1
  N43: 7_Segment4.Segment_D, R34.Pin_1
  N44: 7_Segment4.Segment_DP, R33.Pin_1
  N45: 7_Segment4.Segment_C, R32.Pin_1
  N46: 7_Segment4.Segment_B, R31.Pin_1
  N47: 7_Segment4.Segment_A, R30.Pin_1
  N48: R1.Pin_1, J3.pin1, J3.pin2
  N49: Q3.B, R11.Pin_0
  N50: Q3.C, R3.Pin_0
  N51: Q4.B, R10.Pin_0
  N52: Q4.C, R4.Pin_0
  N53: Q5.B, R14.Pin_0
  N54: Q5.C, R5.Pin_0
  N55: Q6.B, R12.Pin_0
  N56: Q6.C, R7.Pin_0
  N57: Q7.B, R13.Pin_0
  N58: Q7.C, R6.Pin_0
  N59: Q8.B, R15.Pin_0
  N60: Q8.C, R30.Pin_0
  N61: Q9.B, R16.Pin_0
  N62: Q9.C, R31.Pin_0
  N63: Q10.B, R17.Pin_0
  N64: Q10.C, R32.Pin_0
  N65: Q11.B, R18.Pin_0
  N66: Q11.C, R33.Pin_0
  N67: Q12.B, R19.Pin_0
  N68: Q12.C, R34.Pin_0
  N69: Q13.B, R20.Pin_0
  N70: Q13.C, R35.Pin_0
  N71: Q14.B, R21.Pin_0
  N72: Q14.C, R36.Pin_0
  N73: Q15.B, R22.Pin_0
  N74: Q15.C, R37.Pin_0
  N75: Q16.B, R23.Pin_0
  N76: Q16.C, R38.Pin_0
  N77: Q17.B, R24.Pin_0
  N78: Q17.C, R39.Pin_0
  N79: Q18.B, R25.Pin_0
  N80: Q18.C, R40.Pin_0
  N81: Q19.B, R26.Pin_0
  N82: Q19.C, R41.Pin_0
  N83: Q20.B, R27.Pin_0
  N84: Q20.C, R42.Pin_0
  N85: Q21.B, R28.Pin_0
  N86: Q21.C, R43.Pin_0
  N87: Q22.B, R29.Pin_0
  N88: Q22.C, R44.Pin_0
